// Logisim project curcuit.circ as structural Verilog: 11 circuits, main circuit main
module main (
);

  wire clck, clock_1_out, dipswitch_1_sw1, HLT, reset;
  wire [2:0] cpu_1_o0ds;

  and and_1 (clck, clock_1_out, dipswitch_1_sw1);
  Clock clock_1 (.out(clock_1_out));
  DipSwitch #(.number(2)) dipswitch_1 (.sw1(dipswitch_1_sw1), .sw2(HLT));
  Button R (.out(reset));
  CPU cpu_1 (.HLT(HLT), .reset(reset), .clock(clck), .O0DS(cpu_1_o0ds));  // open: O0D0, O0D1, O0D2
  Decoder #(.select(3)) decoder_1 (
    .sel(cpu_1_o0ds), .en(1'b1));  // open: out0, out1, out2, out3, out4, out5, out6, out7
endmodule

module CPU (
  input  clock,
  input  HLT,
  input  reset,
  output [2:0] O0DS,
  output [31:0] O0D0,
  output [31:0] O0D1,
  output [31:0] O0D2
);

  wire ALU_calc, ALU_out, and_1_out, and_4_out, button_1_out, cpu_clock, cpu_HLT, HLT_t,
       instruction_decoder_1_iocs, ioinstrunction_decoder_1_cont, ioinstrunction_decoder_1_mem_o,
       ioinstrunction_decoder_1_set_adr, IR_I, IR_O, jump, N_clock, not_1_out, not_2_out, not_3_out,
       not_4_out, num1_in, num1_out, num2_in, num2_out, O0D0_t, O0D1_t, O0D2_t, O0DS_t, or_1_out, or_2_out,
       or_4_out, or_5_out, PC_out, PC_up, R0_in, R0_out, R1_in, R1_out, R2_in, R2_out, RAM_adr_in, RAM_in,
       RAM_out, reset_SBC, reset_t;
  wire [1:0] alu_1_carry_out, CPU_flaga, instruction_decoder_1_iocsp;
  wire [2:0] bit_extender_5_out, SBC;
  wire [3:0] ALU_inst;
  wire [4:0] IODA;
  wire [22:0] bit_extender_1_out, bit_extender_3_out, ioinstrunction_decoder_1_m_adr, MemAdrReg_q,
       MicroCodePC_p1, multiplexer_1_out, PCD, programcounter_1_p1;
  wire [31:0] alu_1_num_out, bit_extender_2_out, bit_extender_4_out, cpu_Bus, IRD, Mem_Bus, N1D, N2D, R0D,
       R1D, R2D, RAD;

  or or_1 (or_1_out, ioinstrunction_decoder_1_mem_o, RAM_out);
  LedBar #(.matrixcols(23)) ledbar_1 (
    .led0(PCD[0]), .led1(PCD[1]), .led2(PCD[2]), .led3(PCD[3]), .led4(PCD[4]), .led5(PCD[5]), .led6(PCD[6]),
    .led7(PCD[7]), .led8(PCD[8]), .led9(PCD[9]), .led10(PCD[10]), .led11(PCD[11]), .led12(PCD[12]),
    .led13(PCD[13]), .led14(PCD[14]), .led15(PCD[15]), .led16(PCD[16]), .led17(PCD[17]), .led18(PCD[18]),
    .led19(PCD[19]), .led20(PCD[20]), .led21(PCD[21]), .led22(PCD[22]));
  LedBar #(.matrixcols(32)) ledbar_2 (
    .led0(cpu_Bus[0]), .led1(cpu_Bus[1]), .led2(cpu_Bus[2]), .led3(cpu_Bus[3]), .led4(cpu_Bus[4]),
    .led5(cpu_Bus[5]), .led6(cpu_Bus[6]), .led7(cpu_Bus[7]), .led8(cpu_Bus[8]), .led9(cpu_Bus[9]),
    .led10(cpu_Bus[10]), .led11(cpu_Bus[11]), .led12(cpu_Bus[12]), .led13(cpu_Bus[13]), .led14(cpu_Bus[14]),
    .led15(cpu_Bus[15]), .led16(cpu_Bus[16]), .led17(cpu_Bus[17]), .led18(cpu_Bus[18]), .led19(cpu_Bus[19]),
    .led20(cpu_Bus[20]), .led21(cpu_Bus[21]), .led22(cpu_Bus[22]), .led23(cpu_Bus[23]), .led24(cpu_Bus[24]),
    .led25(cpu_Bus[25]), .led26(cpu_Bus[26]), .led27(cpu_Bus[27]), .led28(cpu_Bus[28]), .led29(cpu_Bus[29]),
    .led30(cpu_Bus[30]), .led31(cpu_Bus[31]));
  LedBar #(.matrixcols(32)) ledbar_3 (
    .led0(N1D[0]), .led1(N1D[1]), .led2(N1D[2]), .led3(N1D[3]), .led4(N1D[4]), .led5(N1D[5]), .led6(N1D[6]),
    .led7(N1D[7]), .led8(N1D[8]), .led9(N1D[9]), .led10(N1D[10]), .led11(N1D[11]), .led12(N1D[12]),
    .led13(N1D[13]), .led14(N1D[14]), .led15(N1D[15]), .led16(N1D[16]), .led17(N1D[17]), .led18(N1D[18]),
    .led19(N1D[19]), .led20(N1D[20]), .led21(N1D[21]), .led22(N1D[22]), .led23(N1D[23]), .led24(N1D[24]),
    .led25(N1D[25]), .led26(N1D[26]), .led27(N1D[27]), .led28(N1D[28]), .led29(N1D[29]), .led30(N1D[30]),
    .led31(N1D[31]));
  LedBar #(.matrixcols(32)) ledbar_4 (
    .led0(N2D[0]), .led1(N2D[1]), .led2(N2D[2]), .led3(N2D[3]), .led4(N2D[4]), .led5(N2D[5]), .led6(N2D[6]),
    .led7(N2D[7]), .led8(N2D[8]), .led9(N2D[9]), .led10(N2D[10]), .led11(N2D[11]), .led12(N2D[12]),
    .led13(N2D[13]), .led14(N2D[14]), .led15(N2D[15]), .led16(N2D[16]), .led17(N2D[17]), .led18(N2D[18]),
    .led19(N2D[19]), .led20(N2D[20]), .led21(N2D[21]), .led22(N2D[22]), .led23(N2D[23]), .led24(N2D[24]),
    .led25(N2D[25]), .led26(N2D[26]), .led27(N2D[27]), .led28(N2D[28]), .led29(N2D[29]), .led30(N2D[30]),
    .led31(N2D[31]));
  LedBar #(.matrixcols(32)) ledbar_5 (
    .led0(RAD[0]), .led1(RAD[1]), .led2(RAD[2]), .led3(RAD[3]), .led4(RAD[4]), .led5(RAD[5]), .led6(RAD[6]),
    .led7(RAD[7]), .led8(RAD[8]), .led9(RAD[9]), .led10(RAD[10]), .led11(RAD[11]), .led12(RAD[12]),
    .led13(RAD[13]), .led14(RAD[14]), .led15(RAD[15]), .led16(RAD[16]), .led17(RAD[17]), .led18(RAD[18]),
    .led19(RAD[19]), .led20(RAD[20]), .led21(RAD[21]), .led22(RAD[22]), .led23(RAD[23]), .led24(RAD[24]),
    .led25(RAD[25]), .led26(RAD[26]), .led27(RAD[27]), .led28(RAD[28]), .led29(RAD[29]), .led30(RAD[30]),
    .led31(RAD[31]));
  LedBar #(.matrixcols(9)) ledbar_6 (
    .led0(IRD[0]), .led1(IRD[1]), .led2(IRD[2]), .led3(IRD[3]), .led4(IRD[4]), .led5(IRD[5]), .led6(IRD[6]),
    .led7(IRD[7]), .led8(IRD[8]));
  LedBar #(.matrixcols(32)) ledbar_7 (
    .led0(R0D[0]), .led1(R0D[1]), .led2(R0D[2]), .led3(R0D[3]), .led4(R0D[4]), .led5(R0D[5]), .led6(R0D[6]),
    .led7(R0D[7]), .led8(R0D[8]), .led9(R0D[9]), .led10(R0D[10]), .led11(R0D[11]), .led12(R0D[12]),
    .led13(R0D[13]), .led14(R0D[14]), .led15(R0D[15]), .led16(R0D[16]), .led17(R0D[17]), .led18(R0D[18]),
    .led19(R0D[19]), .led20(R0D[20]), .led21(R0D[21]), .led22(R0D[22]), .led23(R0D[23]), .led24(R0D[24]),
    .led25(R0D[25]), .led26(R0D[26]), .led27(R0D[27]), .led28(R0D[28]), .led29(R0D[29]), .led30(R0D[30]),
    .led31(R0D[31]));
  LedBar #(.matrixcols(32)) ledbar_8 (
    .led0(R1D[0]), .led1(R1D[1]), .led2(R1D[2]), .led3(R1D[3]), .led4(R1D[4]), .led5(R1D[5]), .led6(R1D[6]),
    .led7(R1D[7]), .led8(R1D[8]), .led9(R1D[9]), .led10(R1D[10]), .led11(R1D[11]), .led12(R1D[12]),
    .led13(R1D[13]), .led14(R1D[14]), .led15(R1D[15]), .led16(R1D[16]), .led17(R1D[17]), .led18(R1D[18]),
    .led19(R1D[19]), .led20(R1D[20]), .led21(R1D[21]), .led22(R1D[22]), .led23(R1D[23]), .led24(R1D[24]),
    .led25(R1D[25]), .led26(R1D[26]), .led27(R1D[27]), .led28(R1D[28]), .led29(R1D[29]), .led30(R1D[30]),
    .led31(R1D[31]));
  LedBar #(.matrixcols(32)) ledbar_9 (
    .led0(R2D[0]), .led1(R2D[1]), .led2(R2D[2]), .led3(R2D[3]), .led4(R2D[4]), .led5(R2D[5]), .led6(R2D[6]),
    .led7(R2D[7]), .led8(R2D[8]), .led9(R2D[9]), .led10(R2D[10]), .led11(R2D[11]), .led12(R2D[12]),
    .led13(R2D[13]), .led14(R2D[14]), .led15(R2D[15]), .led16(R2D[16]), .led17(R2D[17]), .led18(R2D[18]),
    .led19(R2D[19]), .led20(R2D[20]), .led21(R2D[21]), .led22(R2D[22]), .led23(R2D[23]), .led24(R2D[24]),
    .led25(R2D[25]), .led26(R2D[26]), .led27(R2D[27]), .led28(R2D[28]), .led29(R2D[29]), .led30(R2D[30]),
    .led31(R2D[31]));
  Multiplexer #(.width(23)) multiplexer_1 (
    .in0(MemAdrReg_q), .in1(ioinstrunction_decoder_1_m_adr), .out(multiplexer_1_out),
    .sel(ioinstrunction_decoder_1_set_adr));
  and and_1 (and_1_out, RAM_in, not_1_out);
  not not_1 (not_1_out, cpu_HLT);
  Bit_Extender #(.in_width(32), .out_width(23), .\type ("zero")) bit_extender_1 (
    .in(cpu_Bus), .out(bit_extender_1_out));
  LedBar #(.matrixcols(23)) ledbar_10 (
    .led0(IRD[9]), .led1(IRD[10]), .led2(IRD[11]), .led3(IRD[12]), .led4(IRD[13]), .led5(IRD[14]),
    .led6(IRD[15]), .led7(IRD[16]), .led8(IRD[17]), .led9(IRD[18]), .led10(IRD[19]), .led11(IRD[20]),
    .led12(IRD[21]), .led13(IRD[22]), .led14(IRD[23]), .led15(IRD[24]), .led16(IRD[25]), .led17(IRD[26]),
    .led18(IRD[27]), .led19(IRD[28]), .led20(IRD[29]), .led21(IRD[30]), .led22(IRD[31]));
  Register #(.width(23)) MemAdrReg (
    .D(bit_extender_3_out), .en(RAM_adr_in), .clk(cpu_clock), .Q(MemAdrReg_q), .clr(reset_t));
  RAM #(.addrWidth(23), .dataWidth(32)) MainRAM (
    .addr(multiplexer_1_out), .we(and_1_out), .oe(or_1_out), .clk(N_clock), .din(cpu_Bus), .dout(Mem_Bus));
  assign bit_extender_2_out = {{9{1'b0}}, PCD};  // Bit_Extender bit_extender_2
  // ProgramCounter PC: pin names not known; wires that end beside it: PCD
  Multiplexer #(.width(32)) multiplexer_2 (.in1(bit_extender_2_out), .out(cpu_Bus), .sel(PC_out));  // open: in0
  Bit_Extender #(.in_width(32), .out_width(23), .\type ("zero")) bit_extender_3 (
    .in(cpu_Bus), .out(bit_extender_3_out));
  Multiplexer #(.width(32)) multiplexer_3 (
    .in1(Mem_Bus),
    .out({cpu_Bus[0], cpu_Bus[1], cpu_Bus[2], cpu_Bus[3], cpu_Bus[4], cpu_Bus[5], cpu_Bus[6], cpu_Bus[7], cpu_Bus[8], cpu_Bus[9], cpu_Bus[10], cpu_Bus[11], cpu_Bus[12], cpu_Bus[13], cpu_Bus[14], cpu_Bus[15], cpu_Bus[16], cpu_Bus[17], cpu_Bus[18], cpu_Bus[19], cpu_Bus[20], cpu_Bus[21], cpu_Bus[22], cpu_Bus[23], cpu_Bus[24], cpu_Bus[25], cpu_Bus[26], cpu_Bus[27], cpu_Bus[28], cpu_Bus[29], cpu_Bus[30], cpu_Bus[31]}),
    .sel(RAM_out));  // open: in0
  Multiplexer #(.width(32)) multiplexer_4 (.in1(bit_extender_4_out), .out(cpu_Bus), .sel(IR_O));  // open: in0
  Multiplexer #(.width(32)) multiplexer_5 (.in1(N1D), .out(cpu_Bus), .sel(num1_out));  // open: in0
  Register #(.width(32)) N2Reg (.D(cpu_Bus), .en(num2_in), .clk(cpu_clock), .Q(N2D), .clr(reset_t));
  Register #(.width(32)) InstReg (.D(cpu_Bus), .en(IR_I), .clk(cpu_clock), .Q(IRD), .clr(reset_t));
  assign bit_extender_4_out = {{9{1'b0}}, {IRD[9], IRD[10], IRD[11], IRD[12], IRD[13], IRD[14], IRD[15], IRD[16], IRD[17], IRD[18], IRD[19], IRD[20], IRD[21], IRD[22], IRD[23], IRD[24], IRD[25], IRD[26], IRD[27], IRD[28], IRD[29], IRD[30], IRD[31]}};  // Bit_Extender bit_extender_4
  Register #(.width(32)) N1Reg (.D(cpu_Bus), .en(num1_in), .clk(cpu_clock), .Q(N1D), .clr(reset_t));
  Multiplexer #(.width(32)) multiplexer_6 (.in1(N2D), .out(cpu_Bus), .sel(num2_out));  // open: in0
  Register #(.width(3)) O0DSR (.D(bit_extender_5_out), .en(O0DS_t), .clk(N_clock), .Q(O0DS), .clr(reset_t));
  Bit_Extender #(.in_width(32), .out_width(3), .\type ("zero")) bit_extender_5 (.in(Mem_Bus), .out(bit_extender_5_out));
  Button button_1 (.out(button_1_out));
  or or_2 (or_2_out, HLT_t, HLT);
  not not_2 (not_2_out, or_2_out);
  not not_3 (not_3_out, cpu_HLT);
  or or_3 (reset_t, button_1_out, reset);
  IOinstrunction_decoder ioinstrunction_decoder_1 (
    .a(IODA), .cstm_instcyc(instruction_decoder_1_iocsp), .cpu_HLT(cpu_HLT),
    .M_adr(ioinstrunction_decoder_1_m_adr), .SET_ADR(ioinstrunction_decoder_1_set_adr),
    .Mem_O(ioinstrunction_decoder_1_mem_o), .cont(ioinstrunction_decoder_1_cont), .O0DS(O0DS_t),
    .O0D0(O0D0_t), .O0D1(O0D1_t), .O0D2(O0D2_t));
  and and_2 (N_clock, clock, not_2_out);
  and and_3 (cpu_clock, N_clock, not_3_out);
  ALU alu_1 (
    .instruction(ALU_inst), .num1(N1D), .num2(N2D), .borrow_in(1'b0), .carry_in(1'b0),
    .mul_carry_in({32{1'b0}}), .div_upper({32{1'b0}}), .carry_out(alu_1_carry_out[0]),
    .comp_out(alu_1_carry_out[1]), .num_out(alu_1_num_out));  // open: borrow_out
  Register #(.width(32)) O0D0R (.D(Mem_Bus), .en(O0D0_t), .clk(N_clock), .Q(O0D0), .clr(reset_t));
  or or_4 (or_4_out, reset_SBC, reset_t);
  Register #(.width(2)) CPUFlags (.D(alu_1_carry_out), .en(ALU_calc), .clk(cpu_clock), .Q(CPU_flaga), .clr(reset_t));
  instruction_decoder instruction_decoder_1 (
    .instruction({IRD[0], IRD[1], IRD[2], IRD[3], IRD[4], IRD[5], IRD[6], IRD[7], IRD[8]}), .sub_stage(SBC),
    .carry(CPU_flaga[0]), .comp(CPU_flaga[1]), .RSC(reset_SBC), .MA_In(RAM_adr_in), .M_I(RAM_in),
    .M_O(RAM_out), .IR_I(IR_I), .IR_O(IR_O), .PC_O(PC_out), .PC_Up(PC_up), .PC_jmp(jump),
    .ALU_inst(ALU_inst), .A_I(ALU_calc), .A_O(ALU_out), .N1_I(num1_in), .N1_O(num1_out), .N2_I(num2_in),
    .N2_O(num2_out), .R0I(R0_in), .R0O(R0_out), .R1I(R1_in), .R1O(R1_out), .R2I(R2_in), .R2O(R2_out),
    .HLT(HLT_t), .IOCS(instruction_decoder_1_iocs), .IOCSP(instruction_decoder_1_iocsp));
  Register #(.width(32)) u_ALU_out (.D(alu_1_num_out), .en(ALU_calc), .clk(cpu_clock), .Q(RAD), .clr(reset_t));
  Multiplexer #(.width(32)) multiplexer_7 (.in1(RAD), .out(cpu_Bus), .sel(ALU_out));  // open: in0
  Bit_Extender #(.in_width(23), .out_width(3)) bit_extender_6 (.in(MicroCodePC_p1), .out(SBC));
  // ProgramCounter MicroCodePC: pin names not known; wires that end beside it: MicroCodePC_p1
  Register #(.width(1)) register_1 (
    .D(instruction_decoder_1_iocs), .en(cpu_clock), .clk(cpu_clock), .Q(cpu_HLT), .clr(or_5_out));
  Register #(.width(32)) O0D1R (.D(Mem_Bus), .en(O0D1_t), .clk(N_clock), .Q(O0D1), .clr(reset_t));
  LedBar #(.matrixcols(3)) ledbar_11 (.led0(SBC[2]), .led1(SBC[1]), .led2(SBC[0]));
  not not_4 (not_4_out, cpu_HLT);
  Multiplexer #(.width(32)) multiplexer_8 (.in1(R0D), .out(cpu_Bus), .sel(R0_out));  // open: in0
  Register #(.width(32)) R0Reg (.D(cpu_Bus), .en(R0_in), .clk(cpu_clock), .Q(R0D), .clr(reset_t));
  Multiplexer #(.width(32)) multiplexer_9 (.in1(R1D), .out(cpu_Bus), .sel(R1_out));  // open: in0
  Register #(.width(32)) R1Reg (.D(cpu_Bus), .en(R1_in), .clk(cpu_clock), .Q(R1D), .clr(reset_t));
  Multiplexer #(.width(32)) multiplexer_10 (.in1(R2D), .out(cpu_Bus), .sel(R2_out));  // open: in0
  Register #(.width(32)) R2Reg (.D(cpu_Bus), .en(R2_in), .clk(cpu_clock), .Q(R2D), .clr(reset_t));
  Register #(.width(32)) O0D2R (.D(Mem_Bus), .en(O0D2_t), .clk(N_clock), .Q(O0D2), .clr(reset_t));
  Bit_Extender #(.in_width(23), .out_width(5), .\type ("zero")) bit_extender_7 (.in(programcounter_1_p1), .out(IODA));
  // ProgramCounter programcounter_1: pin names not known; wires that end beside it: programcounter_1_p1
  and and_4 (and_4_out, IODA[4], IODA[3], IODA[2], IODA[1], IODA[0]);
  or or_5 (or_5_out, ioinstrunction_decoder_1_cont, reset_t, and_4_out);

  // Notes on the sheet:
  //   Program Counter
  //   BUS
  //   RN1
  //   RN2
  //   RA
  //   IR
  //   R0
  //   R1
  //   R2
endmodule

module ALU (
  input  [3:0] instruction,
  input  [31:0] num1,
  input  [31:0] num2,
  input  borrow_in,
  input  carry_in,
  input  [31:0] mul_carry_in,
  input  [31:0] div_upper,
  output carry_out,
  output borrow_out,
  output comp_out,
  output [31:0] num_out
);

  wire comparator_1_eq, comparator_1_gt, comparator_1_lt, comparator_2_eq, comparator_2_gt, comparator_2_lt,
       fpcomparator_1_p3, fpcomparator_1_p4, fpcomparator_1_p5, or_1_out, or_2_out, or_3_out, or_4_out,
       or_5_out, or_6_out;
  wire [31:0] adder_1_out, divider_1_out, divider_2_out, fpadder_1_out, fpdivider_1_out, fpmultiplier_1_out,
       fpnegator_1_p2, fpsubtractor_1_out, fptoint_1_p2, inttofp_1_p2, inttofp_2_p2, multiplier_1_out,
       multiplier_2_out, negator_1_out, subtractor_1_out;

  Adder #(.width(32)) adder_1 (.a(num2), .b(num1), .out(adder_1_out), .cin(carry_in), .cout(carry_out));
  Subtractor #(.width(32)) subtractor_1 (
    .a(num2), .b(num1), .out(subtractor_1_out), .bin(borrow_in), .bout(borrow_out));
  Multiplier #(.width(32)) multiplier_1 (.a(num2), .b(num1), .out(multiplier_1_out), .cin(mul_carry_in));  // open: cout
  Multiplier #(.mode("twosComplement"), .width(32)) multiplier_2 (
    .a(num2), .b(num1), .out(multiplier_2_out), .cin(mul_carry_in));  // open: cout
  Divider #(.width(32)) divider_1 (.a(num2), .b(num1), .out(divider_1_out), .upper(div_upper));  // open: rem
  Divider #(.mode("twosComplement"), .width(32)) divider_2 (
    .a(num2), .b(num1), .out(divider_2_out), .upper(div_upper));  // open: rem
  Negator #(.width(32)) negator_1 (.in(num1), .out(negator_1_out));
  // IntToFP #(.mode("unsigned"), .width(32)) inttofp_1: pin names not known; wires that end beside it: num1, inttofp_1_p2
  // IntToFP #(.width(32)) inttofp_2: pin names not known; wires that end beside it: num1, inttofp_2_p2
  // FPToInt #(.width(32)) fptoint_1: pin names not known; wires that end beside it: num1, fptoint_1_p2
  Comparator #(.mode("unsigned"), .width(32)) comparator_1 (
    .a(num2), .b(num1), .gt(comparator_1_gt), .eq(comparator_1_eq), .lt(comparator_1_lt));
  Comparator #(.width(32)) comparator_2 (
    .a(num2), .b(num1), .gt(comparator_2_gt), .eq(comparator_2_eq), .lt(comparator_2_lt));
  // FPComparator fpcomparator_1: pin names not known; wires that end beside it: num2, num1, fpcomparator_1_p3, fpcomparator_1_p4, fpcomparator_1_p5
  FPAdder fpadder_1 (.a(num2), .b(num1), .out(fpadder_1_out));
  FPSubtractor fpsubtractor_1 (.a(num2), .b(num1), .out(fpsubtractor_1_out));
  FPMultiplier fpmultiplier_1 (.a(num1), .b(num1), .out(fpmultiplier_1_out));
  FPDivider fpdivider_1 (.a(num2), .b(num1), .out(fpdivider_1_out));
  // FPNegator fpnegator_1: pin names not known; wires that end beside it: num1, fpnegator_1_p2
  or or_1 (or_1_out, comparator_1_eq, comparator_1_gt);
  or or_2 (or_2_out, comparator_1_eq, comparator_1_lt);
  or or_3 (or_3_out, comparator_2_eq, comparator_2_gt);
  or or_4 (or_4_out, comparator_2_eq, comparator_2_lt);
  or or_5 (or_5_out, fpcomparator_1_p4, fpcomparator_1_p3);
  or or_6 (or_6_out, fpcomparator_1_p4, fpcomparator_1_p5);
  Multiplexer #(.select(4), .width(32)) multiplexer_1 (
    .in0(adder_1_out), .in1(subtractor_1_out), .in2(multiplier_1_out), .in3(multiplier_2_out),
    .in4(divider_1_out), .in5(divider_2_out), .in6(negator_1_out), .in7(fpadder_1_out),
    .in8(fpsubtractor_1_out), .in9(fpmultiplier_1_out), .in10(fpdivider_1_out), .in11(fpnegator_1_p2),
    .in12(inttofp_1_p2), .in13(inttofp_2_p2), .in14(fptoint_1_p2), .out(num_out), .sel(instruction));  // open: in15
  Multiplexer #(.select(4)) multiplexer_2 (
    .in0(comparator_1_gt), .in1(comparator_1_eq), .in2(comparator_1_lt), .in3(comparator_2_gt),
    .in4(comparator_2_eq), .in5(comparator_2_lt), .in6(fpcomparator_1_p3), .in7(fpcomparator_1_p4),
    .in8(fpcomparator_1_p5), .in9(or_1_out), .in10(or_2_out), .in11(or_3_out), .in12(or_4_out),
    .in13(or_5_out), .in14(or_6_out), .out(comp_out), .sel(instruction));  // open: in15
endmodule

module instruction_decoder (
  input  [8:0] instruction,
  input  [2:0] sub_stage,
  input  carry,
  input  comp,
  output RSC,
  output MA_In,
  output M_I,
  output M_O,
  output IR_I,
  output IR_O,
  output PC_O,
  output PC_Up,
  output PC_jmp,
  output [3:0] ALU_inst,
  output A_I,
  output A_O,
  output N1_I,
  output N1_O,
  output N2_I,
  output N2_O,
  output R0I,
  output R0O,
  output R1I,
  output R1O,
  output R2I,
  output R2O,
  output HLT,
  output IOCS,
  output [1:0] IOCSP
);

  wire and_1_out, and_2_out, and_3_out, and_4_out, and_5_out, and_6_out, and_7_out, and_8_out, and_9_out,
       and_10_out, and_11_out, and_12_out, and_13_out, and_14_out, and_15_out, and_16_out, and_17_out,
       and_18_out, and_19_out, and_20_out, and_21_out, and_22_out, and_23_out, and_24_out, and_25_out,
       and_26_out, and_27_out, and_28_out, and_29_out, and_30_out, and_31_out, and_32_out, and_33_out,
       and_34_out, and_35_out, and_36_out, and_37_out, and_38_out, and_39_out, and_40_out, and_41_out,
       and_42_out, and_44_out, and_45_out, and_46_out, and_47_out, and_48_out, and_49_out, and_50_out,
       and_51_out, and_52_out, and_53_out, and_54_out, and_56_out, and_57_out, and_58_out, and_59_out,
       and_60_out, and_61_out, and_62_out, and_63_out, and_64_out, and_65_out, and_66_out, and_67_out,
       and_68_out, and_69_out, and_70_out, and_71_out, and_72_out, and_73_out, and_74_out, and_75_out,
       and_76_out, and_77_out, and_78_out, and_79_out, and_80_out, and_81_out, and_82_out, and_83_out,
       and_84_out, and_85_out, and_86_out, and_87_out, and_88_out, and_89_out, and_90_out, and_91_out,
       and_92_out, and_93_out, and_94_out, and_95_out, and_96_out, and_97_out, and_98_out, and_99_out,
       and_100_out, and_101_out, and_102_out, and_103_out, and_104_out, and_105_out, and_106_out,
       and_107_out, and_108_out, and_109_out, and_110_out, and_111_out, and_112_out, and_113_out,
       and_114_out, and_115_out, and_116_out, and_117_out, and_118_out, and_119_out, and_120_out,
       and_121_out, and_122_out, and_123_out, and_124_out, and_125_out, and_126_out, and_127_out, not_1_out,
       not_2_out, not_3_out, not_4_out, not_5_out, not_6_out, not_7_out, not_8_out, not_9_out, not_10_out,
       not_11_out, not_12_out, not_13_out, not_14_out;

  not not_1 (not_1_out, instruction[8]);
  not not_2 (not_2_out, instruction[7]);
  not not_3 (not_3_out, instruction[6]);
  not not_4 (not_4_out, instruction[5]);
  not not_5 (not_5_out, instruction[4]);
  not not_6 (not_6_out, instruction[3]);
  not not_7 (not_7_out, instruction[2]);
  not not_8 (not_8_out, instruction[1]);
  not not_9 (not_9_out, instruction[0]);
  not not_10 (not_10_out, sub_stage[2]);
  not not_11 (not_11_out, sub_stage[1]);
  not not_12 (not_12_out, sub_stage[0]);
  not not_13 (not_13_out, carry);
  not not_14 (not_14_out, comp);
  and and_1 (and_1_out, sub_stage[2], sub_stage[1], sub_stage[0]);
  and and_2 (and_2_out, not_1_out, not_2_out, not_3_out, not_4_out, not_5_out, not_6_out, instruction[2], instruction[1], instruction[0], not_10_out, sub_stage[1], not_12_out);
  and and_3 (and_3_out, not_1_out, not_2_out, not_3_out, not_4_out, not_5_out, instruction[3], not_7_out, not_8_out, instruction[0], sub_stage[2], sub_stage[0]);
  and and_4 (and_4_out, not_1_out, not_2_out, not_3_out, not_4_out, not_5_out, instruction[3], not_7_out, instruction[1], sub_stage[2], not_11_out, not_12_out);
  and and_5 (and_5_out, not_1_out, not_2_out, not_3_out, not_4_out, not_5_out, instruction[3], not_8_out, not_9_out, sub_stage[2], not_11_out, not_12_out);
  and and_6 (and_6_out, not_1_out, not_2_out, not_4_out, instruction[4], instruction[3], not_7_out, not_8_out, sub_stage[1], sub_stage[0]);
  and and_7 (and_7_out, not_1_out, not_2_out, not_4_out, instruction[4], instruction[3], not_7_out, not_9_out, sub_stage[1], sub_stage[0]);
  and and_8 (and_8_out, not_1_out, not_2_out, not_4_out, instruction[4], instruction[3], not_8_out, not_9_out, sub_stage[1], sub_stage[0]);
  and and_9 (and_9_out, not_1_out, not_2_out, not_3_out, instruction[5], not_5_out, sub_stage[1], sub_stage[0]);
  and and_10 (and_10_out, not_1_out, not_2_out, not_3_out, instruction[5], not_6_out, not_7_out, not_8_out, sub_stage[1], sub_stage[0]);
  and and_11 (and_11_out, not_1_out, not_2_out, not_3_out, instruction[5], instruction[4], not_6_out, not_7_out, instruction[1], not_9_out, not_10_out, sub_stage[1], not_13_out);
  and and_12 (and_12_out, not_1_out, not_2_out, not_3_out, instruction[4], not_6_out, not_7_out, instruction[1], sub_stage[2], not_11_out, not_12_out);
  and and_13 (and_13_out, not_1_out, not_2_out, not_3_out, instruction[5], instruction[4], not_6_out, not_7_out, instruction[1], instruction[0], not_10_out, sub_stage[1], carry);
  and and_14 (and_14_out, not_1_out, not_2_out, not_3_out, instruction[5], instruction[4], not_6_out, instruction[2], not_8_out, not_9_out, not_10_out, sub_stage[1], not_14_out);
  and and_15 (and_15_out, not_1_out, not_2_out, not_3_out, instruction[4], not_6_out, instruction[2], not_8_out, sub_stage[2], not_11_out, not_12_out);
  and and_16 (and_16_out, not_1_out, not_2_out, not_3_out, instruction[5], instruction[4], not_6_out, instruction[2], not_8_out, instruction[0], not_10_out, sub_stage[1], comp);
  and and_17 (and_17_out, not_1_out, not_2_out, instruction[6], not_5_out, not_7_out, instruction[1], sub_stage[1], sub_stage[0]);
  and and_18 (and_18_out, not_1_out, not_2_out, instruction[6], not_4_out, instruction[4], not_7_out, not_8_out, sub_stage[1], sub_stage[0]);
  and and_19 (and_19_out, not_1_out, not_2_out, instruction[6], not_4_out, not_6_out, not_7_out, instruction[0], sub_stage[1], sub_stage[0]);
  and and_20 (and_20_out, not_1_out, not_2_out, instruction[5], not_5_out, not_6_out, not_7_out, sub_stage[1], sub_stage[0]);
  and and_21 (and_21_out, not_1_out, not_2_out, instruction[6], instruction[5], not_5_out, instruction[3], not_7_out, not_8_out, not_9_out, sub_stage[2], not_11_out, not_12_out);
  and and_22 (and_22_out, not_1_out, not_2_out, instruction[5], not_5_out, not_7_out, instruction[0], sub_stage[1], sub_stage[0]);
  and and_23 (and_23_out, not_1_out, not_2_out, instruction[6], not_4_out, instruction[3], not_8_out, not_9_out, sub_stage[1], sub_stage[0]);
  and and_24 (and_24_out, not_1_out, not_2_out, instruction[6], not_5_out, instruction[3], instruction[2], not_8_out, not_9_out, sub_stage[1], sub_stage[0]);
  and and_25 (and_25_out, not_1_out, not_2_out, not_4_out, not_5_out, not_6_out, instruction[2], not_8_out, not_9_out, sub_stage[1], sub_stage[0]);
  and and_26 (and_26_out, not_1_out, not_2_out, not_3_out, not_5_out, not_6_out, not_8_out, instruction[0], sub_stage[1], sub_stage[0]);
  and and_27 (and_27_out, not_1_out, not_2_out, not_3_out, not_5_out, not_6_out, instruction[1], not_9_out, sub_stage[1], sub_stage[0]);
  and and_28 (and_28_out, not_1_out, not_2_out, not_5_out, not_6_out, not_7_out, instruction[0], sub_stage[1], sub_stage[0]);
  and and_29 (and_29_out, not_1_out, not_2_out, not_3_out, not_4_out, instruction[4], not_6_out, not_7_out, sub_stage[2], not_11_out, not_12_out);
  and and_30 (and_30_out, not_10_out, not_11_out, not_12_out);
  and and_31 (and_31_out, not_1_out, not_2_out, not_3_out, not_4_out, not_5_out, instruction[3], not_7_out, not_8_out, instruction[0], not_10_out, sub_stage[1], sub_stage[0]);
  and and_32 (and_32_out, not_1_out, not_2_out, not_3_out, not_4_out, not_5_out, instruction[3], not_7_out, instruction[1], not_10_out, not_12_out);
  and and_33 (and_33_out, not_1_out, not_2_out, not_3_out, not_4_out, not_5_out, instruction[3], not_8_out, not_9_out, not_10_out, not_12_out);
  and and_34 (and_34_out, not_1_out, not_2_out, not_3_out, not_4_out, instruction[4], not_6_out, not_7_out, instruction[1], not_9_out, sub_stage[1], not_12_out);
  and and_35 (and_35_out, not_1_out, not_2_out, not_3_out, not_4_out, instruction[4], not_6_out, not_7_out, not_10_out, not_12_out);
  and and_36 (and_36_out, not_1_out, not_2_out, not_3_out, not_4_out, instruction[4], not_6_out, not_8_out, not_10_out, not_12_out);
  and and_37 (and_37_out, not_1_out, not_2_out, not_3_out, not_4_out, instruction[4], not_6_out, not_7_out, not_10_out, sub_stage[1], sub_stage[0]);
  and and_38 (and_38_out, not_1_out, not_2_out, not_3_out, not_4_out, instruction[4], not_6_out, not_8_out, not_10_out, sub_stage[1], sub_stage[0]);
  and and_39 (and_39_out, not_10_out, not_11_out, sub_stage[0]);
  and and_40 (and_40_out, not_1_out, not_2_out, not_3_out, not_4_out, not_5_out, instruction[3], not_7_out, not_8_out, instruction[0], sub_stage[2], not_11_out, not_12_out);
  and and_41 (and_41_out, not_1_out, not_2_out, not_3_out, not_4_out, not_5_out, instruction[3], not_7_out, instruction[1], not_10_out, sub_stage[0]);
  and and_42 (and_42_out, not_1_out, not_2_out, not_3_out, not_4_out, not_5_out, instruction[3], not_8_out, not_9_out, not_10_out, sub_stage[0]);
  and and_43 (IR_I, not_10_out, not_11_out, sub_stage[0]);
  and and_44 (and_44_out, not_1_out, not_2_out, not_3_out, not_4_out, instruction[3], not_8_out, not_9_out, not_10_out, sub_stage[1], not_12_out);
  and and_45 (and_45_out, not_1_out, not_2_out, not_3_out, not_4_out, instruction[4], not_7_out, not_10_out, sub_stage[1], not_12_out);
  and and_46 (and_46_out, not_1_out, not_2_out, not_3_out, not_4_out, instruction[4], not_6_out, not_8_out, not_10_out, sub_stage[1], not_12_out);
  and and_47 (and_47_out, not_1_out, not_2_out, not_3_out, instruction[4], not_6_out, not_7_out, not_8_out, instruction[0], not_10_out, sub_stage[1], not_12_out);
  and and_48 (and_48_out, not_1_out, not_2_out, not_3_out, not_4_out, not_5_out, instruction[3], not_7_out, not_8_out, instruction[0], not_10_out, sub_stage[1], sub_stage[0]);
  and and_49 (and_49_out, not_1_out, not_2_out, not_3_out, not_4_out, instruction[4], not_6_out, not_7_out, instruction[1], not_9_out, sub_stage[1], not_12_out);
  and and_50 (and_50_out, not_1_out, not_2_out, not_3_out, not_4_out, instruction[3], not_7_out, instruction[1], not_10_out, sub_stage[1], not_12_out);
  and and_51 (and_51_out, not_1_out, not_2_out, not_3_out, instruction[5], instruction[4], not_6_out, instruction[2], not_8_out, not_9_out, not_10_out, sub_stage[1], comp);
  and and_52 (and_52_out, not_1_out, not_2_out, not_3_out, instruction[5], instruction[4], not_6_out, instruction[2], not_8_out, instruction[0], not_10_out, sub_stage[1], not_14_out);
  and and_53 (and_53_out, not_1_out, not_2_out, not_3_out, instruction[5], instruction[4], not_6_out, not_7_out, instruction[1], not_9_out, not_10_out, sub_stage[1], carry);
  and and_54 (and_54_out, not_1_out, not_2_out, not_3_out, instruction[5], instruction[4], not_6_out, not_7_out, instruction[1], instruction[0], not_10_out, sub_stage[1], not_13_out);
  and and_55 (PC_O, not_10_out, not_11_out, not_12_out);
  and and_56 (and_56_out, not_10_out, not_11_out, sub_stage[0]);
  and and_57 (and_57_out, not_1_out, not_2_out, not_3_out, instruction[5], instruction[4], not_6_out, not_7_out, not_8_out, instruction[0], not_10_out, sub_stage[1], not_12_out);
  and and_58 (and_58_out, not_1_out, not_2_out, not_3_out, instruction[5], instruction[4], not_6_out, not_7_out, instruction[1], not_10_out, sub_stage[0]);
  and and_59 (and_59_out, not_1_out, not_2_out, not_3_out, instruction[5], instruction[4], not_6_out, instruction[2], not_8_out, not_10_out, sub_stage[0]);
  and and_60 (and_60_out, not_1_out, not_2_out, not_3_out, instruction[5], instruction[4], not_6_out, instruction[2], not_8_out, not_9_out, not_10_out, sub_stage[1], comp);
  and and_61 (and_61_out, not_1_out, not_2_out, not_3_out, instruction[5], instruction[4], not_6_out, not_7_out, instruction[1], not_9_out, not_10_out, sub_stage[1], carry);
  and and_62 (and_62_out, not_1_out, not_2_out, not_3_out, instruction[5], instruction[4], not_6_out, not_7_out, not_8_out, instruction[0], not_10_out, sub_stage[1], not_12_out);
  and and_63 (and_63_out, not_1_out, not_2_out, not_3_out, instruction[5], instruction[4], not_6_out, not_7_out, instruction[1], instruction[0], not_10_out, sub_stage[1], not_13_out);
  and and_64 (and_64_out, not_1_out, not_2_out, not_3_out, instruction[5], instruction[4], not_6_out, instruction[2], not_8_out, instruction[0], not_10_out, sub_stage[1], not_14_out);
  and and_65 (and_65_out, not_1_out, not_2_out, not_3_out, instruction[5], not_5_out, not_6_out, instruction[1], not_10_out, sub_stage[1], not_12_out);
  and and_66 (and_66_out, not_1_out, not_2_out, not_3_out, instruction[5], not_5_out, not_6_out, instruction[2], not_10_out, sub_stage[1], not_12_out);
  and and_67 (and_67_out, not_1_out, not_2_out, not_3_out, instruction[5], instruction[4], not_6_out, not_7_out, not_8_out, not_9_out, not_10_out, sub_stage[1], not_12_out);
  and and_68 (and_68_out, not_1_out, not_2_out, not_3_out, instruction[5], not_5_out, not_6_out, instruction[0], not_10_out, sub_stage[1], not_12_out);
  and and_69 (and_69_out, not_1_out, not_2_out, not_3_out, not_5_out, not_6_out, instruction[2], instruction[1], not_10_out, sub_stage[1], not_12_out);
  and and_70 (and_70_out, not_1_out, not_2_out, not_3_out, instruction[5], not_5_out, not_6_out, not_7_out, not_8_out, not_9_out, not_10_out, sub_stage[1], not_12_out);
  and and_71 (and_71_out, not_1_out, not_2_out, not_3_out, instruction[5], not_5_out, instruction[3], instruction[2], not_10_out, sub_stage[1], not_12_out);
  and and_72 (and_72_out, not_1_out, not_2_out, not_3_out, not_5_out, not_6_out, instruction[2], instruction[0], not_10_out, sub_stage[1], not_12_out);
  and and_73 (and_73_out, not_1_out, not_2_out, not_3_out, not_5_out, not_6_out, instruction[2], not_8_out, not_9_out, not_10_out, sub_stage[1], not_12_out);
  and and_74 (and_74_out, not_1_out, not_2_out, not_3_out, instruction[5], not_5_out, not_6_out, not_8_out, not_9_out, not_10_out, sub_stage[1], not_12_out);
  and and_75 (and_75_out, not_1_out, not_2_out, not_3_out, instruction[5], not_5_out, instruction[3], instruction[1], not_10_out, sub_stage[1], not_12_out);
  and and_76 (and_76_out, not_1_out, not_2_out, not_3_out, not_5_out, not_6_out, instruction[1], instruction[0], not_10_out, sub_stage[1], not_12_out);
  and and_77 (and_77_out, not_1_out, not_2_out, not_3_out, not_5_out, not_6_out, instruction[1], not_9_out, not_10_out, sub_stage[1], not_12_out);
  and and_78 (and_78_out, not_1_out, not_2_out, not_3_out, not_5_out, not_6_out, instruction[2], not_9_out, not_10_out, sub_stage[1], not_12_out);
  and and_79 (and_79_out, not_1_out, not_2_out, not_3_out, instruction[5], not_5_out, not_6_out, not_9_out, not_10_out, sub_stage[1], not_12_out);
  and and_80 (and_80_out, not_1_out, not_2_out, not_3_out, instruction[5], not_5_out, instruction[3], instruction[0], not_10_out, sub_stage[1], not_12_out);
  and and_81 (and_81_out, not_1_out, not_2_out, not_3_out, not_5_out, not_6_out, instruction[2], not_8_out, not_10_out, sub_stage[1], not_12_out);
  and and_82 (and_82_out, not_1_out, not_2_out, not_3_out, instruction[5], not_5_out, not_10_out, sub_stage[1], not_12_out);
  and and_83 (and_83_out, not_1_out, not_2_out, not_3_out, instruction[5], not_6_out, not_7_out, not_8_out, not_9_out, not_10_out, sub_stage[1], not_12_out);
  and and_84 (and_84_out, not_1_out, not_2_out, not_3_out, not_5_out, not_6_out, instruction[0], not_10_out, sub_stage[1], not_12_out);
  and and_85 (and_85_out, not_1_out, not_2_out, not_3_out, not_5_out, not_6_out, not_7_out, instruction[1], not_10_out, sub_stage[1], not_12_out);
  and and_86 (and_86_out, not_1_out, not_2_out, instruction[6], instruction[5], not_5_out, instruction[3], not_7_out, instruction[0], not_10_out, sub_stage[1], not_12_out);
  and and_87 (and_87_out, not_1_out, not_2_out, instruction[6], instruction[5], not_5_out, instruction[3], not_7_out, instruction[1], not_10_out, sub_stage[1], not_12_out);
  and and_88 (and_88_out, not_1_out, not_2_out, instruction[6], instruction[5], not_5_out, instruction[3], instruction[2], not_8_out, not_9_out, not_10_out, sub_stage[1], not_12_out);
  and and_89 (and_89_out, not_1_out, not_2_out, not_3_out, not_4_out, instruction[4], not_6_out, instruction[2], not_8_out, instruction[0], not_10_out, sub_stage[1], sub_stage[0]);
  and and_90 (and_90_out, not_1_out, not_2_out, instruction[6], instruction[5], not_5_out, instruction[3], not_7_out, not_8_out, not_9_out, not_10_out, sub_stage[1], sub_stage[0]);
  and and_91 (and_91_out, not_1_out, not_2_out, not_4_out, instruction[4], instruction[3], not_7_out, not_8_out, not_9_out, not_10_out, sub_stage[1], not_12_out);
  and and_92 (and_92_out, not_1_out, not_2_out, instruction[6], not_4_out, instruction[3], not_7_out, not_8_out, not_9_out, not_10_out, sub_stage[1], not_12_out);
  and and_93 (and_93_out, not_1_out, not_2_out, instruction[6], not_4_out, instruction[4], not_7_out, not_8_out, not_9_out, not_10_out, sub_stage[1], not_12_out);
  and and_94 (and_94_out, not_1_out, not_2_out, instruction[6], instruction[5], not_5_out, not_6_out, not_7_out, not_8_out, not_9_out, not_10_out, sub_stage[1], not_12_out);
  and and_95 (and_95_out, not_1_out, not_2_out, not_3_out, not_4_out, not_5_out, instruction[3], not_7_out, not_8_out, not_9_out, not_10_out, sub_stage[1], sub_stage[0]);
  and and_96 (and_96_out, not_1_out, not_2_out, instruction[6], instruction[5], not_5_out, instruction[3], not_7_out, not_8_out, not_9_out, not_10_out, sub_stage[1], sub_stage[0]);
  and and_97 (and_97_out, not_1_out, not_2_out, instruction[6], not_4_out, not_5_out, not_6_out, not_7_out, instruction[0], not_10_out, sub_stage[1], not_12_out);
  and and_98 (and_98_out, not_1_out, not_2_out, instruction[6], not_4_out, not_5_out, not_6_out, not_7_out, instruction[1], not_10_out, sub_stage[1], not_12_out);
  and and_99 (and_99_out, not_1_out, not_2_out, instruction[6], not_4_out, not_5_out, not_6_out, instruction[2], not_8_out, not_9_out, not_10_out, sub_stage[1], not_12_out);
  and and_100 (and_100_out, not_1_out, not_2_out, not_3_out, not_4_out, instruction[4], not_6_out, not_7_out, not_8_out, not_9_out, not_10_out, sub_stage[1], sub_stage[0]);
  and and_101 (and_101_out, not_1_out, not_2_out, not_4_out, instruction[4], instruction[3], not_7_out, not_8_out, instruction[0], not_10_out, sub_stage[1], not_12_out);
  and and_102 (and_102_out, not_1_out, not_2_out, instruction[6], instruction[5], not_5_out, not_7_out, not_8_out, instruction[0], not_10_out, sub_stage[1], not_12_out);
  and and_103 (and_103_out, not_1_out, not_2_out, not_3_out, not_4_out, not_5_out, instruction[3], not_7_out, not_8_out, instruction[0], sub_stage[2], not_11_out, not_12_out);
  and and_104 (and_104_out, not_1_out, not_2_out, instruction[6], not_4_out, not_6_out, not_7_out, not_8_out, instruction[0], not_10_out, sub_stage[1], not_12_out);
  and and_105 (and_105_out, not_1_out, not_2_out, instruction[6], not_4_out, not_5_out, instruction[3], not_7_out, instruction[1], not_10_out, sub_stage[1], not_12_out);
  and and_106 (and_106_out, not_1_out, not_2_out, instruction[6], not_4_out, not_5_out, instruction[3], not_8_out, not_9_out, not_10_out, sub_stage[1], not_12_out);
  and and_107 (and_107_out, not_1_out, not_2_out, not_3_out, not_4_out, instruction[4], not_6_out, not_7_out, not_8_out, instruction[0], not_10_out, sub_stage[1], sub_stage[0]);
  and and_108 (and_108_out, not_1_out, not_2_out, not_4_out, instruction[4], instruction[3], not_7_out, instruction[1], not_9_out, not_10_out, sub_stage[1], not_12_out);
  and and_109 (and_109_out, not_1_out, not_2_out, instruction[6], not_5_out, not_7_out, instruction[1], not_9_out, not_10_out, sub_stage[1], not_12_out);
  and and_110 (and_110_out, not_1_out, not_2_out, not_3_out, not_4_out, not_5_out, instruction[3], not_7_out, instruction[1], not_9_out, not_10_out, sub_stage[1], sub_stage[0]);
  and and_111 (and_111_out, not_1_out, not_2_out, instruction[6], not_4_out, instruction[4], not_6_out, not_7_out, instruction[0], not_10_out, sub_stage[1], not_12_out);
  and and_112 (and_112_out, not_1_out, not_2_out, instruction[6], not_4_out, instruction[4], not_6_out, not_8_out, not_9_out, not_10_out, sub_stage[1], not_12_out);
  and and_113 (and_113_out, not_1_out, not_2_out, not_3_out, not_4_out, instruction[4], not_6_out, not_7_out, instruction[1], not_9_out, not_10_out, sub_stage[1], sub_stage[0]);
  and and_114 (and_114_out, not_1_out, not_2_out, not_3_out, not_4_out, instruction[4], instruction[3], not_7_out, instruction[1], instruction[0], not_10_out, sub_stage[1], not_12_out);
  and and_115 (and_115_out, not_1_out, not_2_out, instruction[6], not_5_out, not_7_out, instruction[1], instruction[0], not_10_out, sub_stage[1], not_12_out);
  and and_116 (and_116_out, not_1_out, not_2_out, instruction[6], not_4_out, not_6_out, not_7_out, instruction[1], instruction[0], not_10_out, sub_stage[1], not_12_out);
  and and_117 (and_117_out, not_1_out, not_2_out, not_3_out, not_4_out, not_5_out, instruction[3], not_7_out, instruction[1], instruction[0], not_10_out, sub_stage[1], sub_stage[0]);
  and and_118 (and_118_out, not_1_out, not_2_out, instruction[6], not_4_out, instruction[4], instruction[3], not_7_out, not_8_out, not_10_out, sub_stage[1], not_12_out);
  and and_119 (and_119_out, not_1_out, not_2_out, instruction[6], not_4_out, instruction[4], instruction[3], not_7_out, not_9_out, not_10_out, sub_stage[1], not_12_out);
  and and_120 (and_120_out, not_1_out, not_2_out, instruction[6], not_4_out, instruction[4], instruction[3], not_8_out, not_9_out, not_10_out, sub_stage[1], not_12_out);
  and and_121 (and_121_out, not_1_out, not_2_out, not_3_out, not_4_out, instruction[4], not_6_out, not_7_out, instruction[1], instruction[0], not_10_out, sub_stage[1], sub_stage[0]);
  and and_122 (and_122_out, not_1_out, not_2_out, not_4_out, instruction[4], instruction[3], instruction[2], not_8_out, not_9_out, not_10_out, sub_stage[1], not_12_out);
  and and_123 (and_123_out, not_1_out, not_2_out, instruction[6], not_4_out, instruction[2], not_8_out, not_9_out, not_10_out, sub_stage[1], not_12_out);
  and and_124 (and_124_out, not_1_out, not_2_out, instruction[6], not_5_out, instruction[3], instruction[2], not_8_out, not_9_out, not_10_out, sub_stage[1], not_12_out);
  and and_125 (and_125_out, not_1_out, not_2_out, not_3_out, not_4_out, not_5_out, instruction[3], instruction[2], not_8_out, not_9_out, not_10_out, sub_stage[1], sub_stage[0]);
  and and_126 (and_126_out, not_1_out, not_2_out, instruction[6], instruction[5], not_5_out, not_6_out, not_7_out, not_10_out, sub_stage[1], not_12_out);
  and and_127 (and_127_out, not_1_out, not_2_out, not_3_out, not_4_out, instruction[4], not_6_out, instruction[2], not_8_out, not_9_out, not_10_out, sub_stage[1], sub_stage[0]);
  and and_128 (HLT, instruction[8], instruction[7], instruction[6], instruction[5], instruction[4], instruction[3], instruction[2], instruction[1], instruction[0], not_10_out, sub_stage[1], not_12_out);
  or or_1 (MA_In, and_30_out, and_31_out, and_32_out, and_33_out, and_34_out, and_35_out, and_36_out);
  or or_2 (M_I, and_37_out, and_38_out);
  or or_3 (M_O, and_39_out, and_40_out, and_41_out, and_42_out);
  or or_4 (PC_Up, and_56_out, and_57_out, and_58_out, and_59_out);
  or or_5 (PC_jmp, and_60_out, and_61_out, and_62_out, and_63_out, and_64_out);
  or or_6 (ALU_inst[3], and_65_out, and_66_out, and_67_out, and_68_out);
  or or_7 (ALU_inst[2], and_69_out, and_70_out, and_71_out, and_72_out);
  or or_8 (ALU_inst[1], and_73_out, and_74_out, and_75_out, and_76_out);
  or or_9 (ALU_inst[0], and_77_out, and_78_out, and_79_out, and_80_out);
  or or_10 (A_I, and_81_out, and_82_out, and_83_out, and_84_out, and_85_out);
  or or_11 (A_O, and_86_out, and_87_out, and_88_out, and_89_out, and_90_out);
  or or_12 (N1_I, and_91_out, and_92_out, and_93_out, and_94_out, and_95_out, and_96_out);
  or or_13 (N1_O, and_97_out, and_98_out, and_99_out, and_100_out);
  or or_14 (N2_I, and_101_out, and_102_out, and_103_out, and_104_out);
  or or_15 (N2_O, and_105_out, and_106_out, and_107_out);
  or or_16 (R0I, and_108_out, and_109_out, and_110_out);
  or or_17 (R0O, and_111_out, and_112_out, and_113_out);
  or or_18 (R1I, and_114_out, and_115_out, and_116_out, and_117_out);
  or or_19 (R1O, and_118_out, and_119_out, and_120_out, and_121_out);
  or or_20 (R2I, and_122_out, and_123_out, and_124_out, and_125_out);
  or or_21 (R2O, and_126_out, and_127_out);
  or or_22 (IR_O, and_44_out, and_45_out, and_46_out, and_47_out, and_48_out, and_49_out, and_50_out, and_51_out, and_52_out, and_53_out, and_54_out);
  or or_23 (RSC, and_1_out, and_2_out, and_3_out, and_4_out, and_5_out, and_6_out, and_7_out, and_8_out, and_9_out, and_10_out, and_11_out, and_12_out, and_13_out, and_14_out, and_15_out, and_16_out, and_17_out, and_18_out, and_19_out, and_20_out, and_21_out, and_22_out, and_23_out, and_24_out, and_25_out, and_26_out, and_27_out, and_28_out, and_29_out);

  assign IOCS = 1'b0;
endmodule

module IOinstrunction_decoder (
  input  [4:0] a,
  input  [1:0] cstm_instcyc,
  input  cpu_HLT,
  output [22:0] M_adr,
  output SET_ADR,
  output Mem_O,
  output cont,
  output O0DS,
  output O0D0,
  output O0D1,
  output O0D2
);
endmodule

module ProgramCounter (
  input  [22:0] JmpAddr,
  input  Reset,
  input  Jmp,
  input  Clock,
  output [22:0] ip
);

  wire [22:0] adder_1_out, multiplexer_1_out;

  Adder #(.width(23)) adder_1 (.a(ip), .b(23'h1), .out(adder_1_out));  // open: cin, cout
  Multiplexer #(.width(23)) multiplexer_1 (.in0(adder_1_out), .in1(JmpAddr), .out(multiplexer_1_out), .sel(Jmp));
  Register #(.width(23)) PC (.D(multiplexer_1_out), .en(1'b1), .Q(ip), .clk(Clock), .clr(Reset));
endmodule

module Vregister (
  input  [31:0] D,
  input  WE,
  input  reset,
  input  C,
  input  [5:0] BG,
  output [31:0] DO
);

  wire [31:0] bit_extender_1_out, bit_extender_2_out, bit_extender_3_out, bit_extender_4_out,
       bit_extender_5_out, bit_extender_6_out, bit_extender_7_out, bit_extender_8_out, bit_extender_9_out,
       bit_extender_10_out, bit_extender_11_out, bit_extender_12_out, bit_extender_13_out,
       bit_extender_14_out, bit_extender_15_out, bit_extender_16_out, bit_extender_17_out,
       bit_extender_18_out, bit_extender_19_out, bit_extender_20_out, bit_extender_21_out,
       bit_extender_22_out, bit_extender_23_out, bit_extender_24_out, bit_extender_25_out,
       bit_extender_26_out, bit_extender_27_out, bit_extender_28_out, bit_extender_29_out,
       bit_extender_30_out, bit_extender_31_out, bit_extender_32_out, bit_extender_33_out,
       bit_extender_34_out, bit_extender_35_out, bit_extender_36_out, bit_extender_37_out,
       bit_extender_38_out, bit_extender_39_out, bit_extender_40_out, bit_extender_41_out,
       bit_extender_42_out, bit_extender_43_out, bit_extender_44_out, bit_extender_45_out,
       bit_extender_46_out, bit_extender_47_out, bit_extender_48_out, bit_extender_49_out,
       bit_extender_50_out, bit_extender_51_out, bit_extender_52_out, bit_extender_53_out,
       bit_extender_54_out, bit_extender_55_out, bit_extender_56_out, bit_extender_57_out,
       bit_extender_58_out, bit_extender_59_out, bit_extender_60_out, bit_extender_61_out,
       bit_extender_62_out, multiplexer_1_out, multiplexer_2_out, register_1_q;

  Register #(.width(32)) register_1 (.D(D), .en(WE), .clk(C), .Q(register_1_q), .clr(reset));
  assign bit_extender_1_out = {{31{1'b0}}, register_1_q[31]};  // Bit_Extender bit_extender_1
  assign bit_extender_2_out = {{31{1'b0}}, register_1_q[30]};  // Bit_Extender bit_extender_2
  assign bit_extender_3_out = {{31{1'b0}}, register_1_q[29]};  // Bit_Extender bit_extender_3
  assign bit_extender_4_out = {{31{1'b0}}, register_1_q[28]};  // Bit_Extender bit_extender_4
  assign bit_extender_5_out = {{31{1'b0}}, register_1_q[27]};  // Bit_Extender bit_extender_5
  assign bit_extender_6_out = {{31{1'b0}}, register_1_q[26]};  // Bit_Extender bit_extender_6
  assign bit_extender_7_out = {{31{1'b0}}, register_1_q[25]};  // Bit_Extender bit_extender_7
  assign bit_extender_8_out = {{31{1'b0}}, register_1_q[24]};  // Bit_Extender bit_extender_8
  assign bit_extender_9_out = {{31{1'b0}}, register_1_q[23]};  // Bit_Extender bit_extender_9
  assign bit_extender_10_out = {{31{1'b0}}, register_1_q[22]};  // Bit_Extender bit_extender_10
  assign bit_extender_11_out = {{31{1'b0}}, register_1_q[21]};  // Bit_Extender bit_extender_11
  assign bit_extender_12_out = {{31{1'b0}}, register_1_q[20]};  // Bit_Extender bit_extender_12
  assign bit_extender_13_out = {{31{1'b0}}, register_1_q[19]};  // Bit_Extender bit_extender_13
  assign bit_extender_14_out = {{31{1'b0}}, register_1_q[18]};  // Bit_Extender bit_extender_14
  assign bit_extender_15_out = {{31{1'b0}}, register_1_q[17]};  // Bit_Extender bit_extender_15
  assign bit_extender_16_out = {{31{1'b0}}, register_1_q[16]};  // Bit_Extender bit_extender_16
  assign bit_extender_17_out = {{31{1'b0}}, register_1_q[15]};  // Bit_Extender bit_extender_17
  assign bit_extender_18_out = {{31{1'b0}}, register_1_q[14]};  // Bit_Extender bit_extender_18
  assign bit_extender_19_out = {{31{1'b0}}, register_1_q[13]};  // Bit_Extender bit_extender_19
  assign bit_extender_20_out = {{31{1'b0}}, register_1_q[12]};  // Bit_Extender bit_extender_20
  assign bit_extender_21_out = {{31{1'b0}}, register_1_q[11]};  // Bit_Extender bit_extender_21
  assign bit_extender_22_out = {{31{1'b0}}, register_1_q[10]};  // Bit_Extender bit_extender_22
  assign bit_extender_23_out = {{31{1'b0}}, register_1_q[9]};  // Bit_Extender bit_extender_23
  assign bit_extender_24_out = {{31{1'b0}}, register_1_q[8]};  // Bit_Extender bit_extender_24
  assign bit_extender_25_out = {{31{1'b0}}, register_1_q[7]};  // Bit_Extender bit_extender_25
  assign bit_extender_26_out = {{31{1'b0}}, register_1_q[6]};  // Bit_Extender bit_extender_26
  assign bit_extender_27_out = {{31{1'b0}}, register_1_q[5]};  // Bit_Extender bit_extender_27
  assign bit_extender_28_out = {{31{1'b0}}, register_1_q[4]};  // Bit_Extender bit_extender_28
  assign bit_extender_29_out = {{31{1'b0}}, register_1_q[3]};  // Bit_Extender bit_extender_29
  assign bit_extender_30_out = {{31{1'b0}}, register_1_q[2]};  // Bit_Extender bit_extender_30
  assign bit_extender_31_out = {{31{1'b0}}, register_1_q[1]};  // Bit_Extender bit_extender_31
  assign bit_extender_32_out = {{31{1'b0}}, register_1_q[0]};  // Bit_Extender bit_extender_32
  assign bit_extender_33_out = {{16{1'b0}}, register_1_q[15:0]};  // Bit_Extender bit_extender_33
  assign bit_extender_34_out = {{16{1'b0}}, register_1_q[31:16]};  // Bit_Extender bit_extender_34
  assign bit_extender_35_out = {{24{1'b0}}, register_1_q[7:0]};  // Bit_Extender bit_extender_35
  assign bit_extender_36_out = {{24{1'b0}}, register_1_q[15:8]};  // Bit_Extender bit_extender_36
  assign bit_extender_37_out = {{24{1'b0}}, register_1_q[23:16]};  // Bit_Extender bit_extender_37
  assign bit_extender_38_out = {{24{1'b0}}, register_1_q[31:24]};  // Bit_Extender bit_extender_38
  assign bit_extender_39_out = {{28{1'b0}}, register_1_q[3:0]};  // Bit_Extender bit_extender_39
  assign bit_extender_40_out = {{28{1'b0}}, register_1_q[7:4]};  // Bit_Extender bit_extender_40
  assign bit_extender_41_out = {{28{1'b0}}, register_1_q[11:8]};  // Bit_Extender bit_extender_41
  assign bit_extender_42_out = {{28{1'b0}}, register_1_q[15:12]};  // Bit_Extender bit_extender_42
  assign bit_extender_43_out = {{28{1'b0}}, register_1_q[19:16]};  // Bit_Extender bit_extender_43
  assign bit_extender_44_out = {{28{1'b0}}, register_1_q[23:20]};  // Bit_Extender bit_extender_44
  assign bit_extender_45_out = {{28{1'b0}}, register_1_q[27:24]};  // Bit_Extender bit_extender_45
  assign bit_extender_46_out = {{28{1'b0}}, register_1_q[31:28]};  // Bit_Extender bit_extender_46
  assign bit_extender_47_out = {{30{1'b0}}, register_1_q[1:0]};  // Bit_Extender bit_extender_47
  assign bit_extender_48_out = {{30{1'b0}}, register_1_q[3:2]};  // Bit_Extender bit_extender_48
  assign bit_extender_49_out = {{30{1'b0}}, register_1_q[5:4]};  // Bit_Extender bit_extender_49
  assign bit_extender_50_out = {{30{1'b0}}, register_1_q[7:6]};  // Bit_Extender bit_extender_50
  assign bit_extender_51_out = {{30{1'b0}}, register_1_q[9:8]};  // Bit_Extender bit_extender_51
  assign bit_extender_52_out = {{30{1'b0}}, register_1_q[11:10]};  // Bit_Extender bit_extender_52
  assign bit_extender_53_out = {{30{1'b0}}, register_1_q[13:12]};  // Bit_Extender bit_extender_53
  assign bit_extender_54_out = {{30{1'b0}}, register_1_q[15:14]};  // Bit_Extender bit_extender_54
  assign bit_extender_55_out = {{30{1'b0}}, register_1_q[17:16]};  // Bit_Extender bit_extender_55
  assign bit_extender_56_out = {{30{1'b0}}, register_1_q[19:18]};  // Bit_Extender bit_extender_56
  assign bit_extender_57_out = {{30{1'b0}}, register_1_q[21:20]};  // Bit_Extender bit_extender_57
  assign bit_extender_58_out = {{30{1'b0}}, register_1_q[23:22]};  // Bit_Extender bit_extender_58
  assign bit_extender_59_out = {{30{1'b0}}, register_1_q[25:24]};  // Bit_Extender bit_extender_59
  assign bit_extender_60_out = {{30{1'b0}}, register_1_q[27:26]};  // Bit_Extender bit_extender_60
  assign bit_extender_61_out = {{30{1'b0}}, register_1_q[29:28]};  // Bit_Extender bit_extender_61
  assign bit_extender_62_out = {{30{1'b0}}, register_1_q[31:30]};  // Bit_Extender bit_extender_62
  Multiplexer #(.select(5), .width(32)) multiplexer_1 (
    .in0(bit_extender_1_out), .in1(bit_extender_2_out), .in2(bit_extender_3_out), .in3(bit_extender_4_out),
    .in4(bit_extender_5_out), .in5(bit_extender_6_out), .in6(bit_extender_7_out), .in7(bit_extender_8_out),
    .in8(bit_extender_9_out), .in9(bit_extender_10_out), .in10(bit_extender_11_out),
    .in11(bit_extender_12_out), .in12(bit_extender_13_out), .in13(bit_extender_14_out),
    .in14(bit_extender_15_out), .in15(bit_extender_16_out), .in16(bit_extender_17_out),
    .in17(bit_extender_18_out), .in18(bit_extender_19_out), .in19(bit_extender_20_out),
    .in20(bit_extender_21_out), .in21(bit_extender_22_out), .in22(bit_extender_23_out),
    .in23(bit_extender_24_out), .in24(bit_extender_25_out), .in25(bit_extender_26_out),
    .in26(bit_extender_27_out), .in27(bit_extender_28_out), .in28(bit_extender_29_out),
    .in29(bit_extender_30_out), .in30(bit_extender_31_out), .in31(bit_extender_32_out),
    .out(multiplexer_1_out), .sel(BG[4:0]));
  Multiplexer #(.select(5), .width(32)) multiplexer_2 (
    .in0(register_1_q), .in1(bit_extender_33_out), .in2(bit_extender_34_out), .in3(bit_extender_35_out),
    .in4(bit_extender_36_out), .in5(bit_extender_37_out), .in6(bit_extender_38_out),
    .in7(bit_extender_39_out), .in8(bit_extender_40_out), .in9(bit_extender_41_out),
    .in10(bit_extender_42_out), .in11(bit_extender_43_out), .in12(bit_extender_44_out),
    .in13(bit_extender_45_out), .in14(bit_extender_46_out), .in15(bit_extender_47_out),
    .in16(bit_extender_48_out), .in17(bit_extender_49_out), .in18(bit_extender_50_out),
    .in19(bit_extender_51_out), .in20(bit_extender_52_out), .in21(bit_extender_53_out),
    .in22(bit_extender_54_out), .in23(bit_extender_55_out), .in24(bit_extender_56_out),
    .in25(bit_extender_57_out), .in26(bit_extender_58_out), .in27(bit_extender_59_out),
    .in28(bit_extender_60_out), .in29(bit_extender_61_out), .in30(bit_extender_62_out),
    .out(multiplexer_2_out), .sel(BG[4:0]));  // open: in31
  Multiplexer #(.width(32)) multiplexer_3 (.in0(multiplexer_2_out), .in1(multiplexer_1_out), .out(DO), .sel(BG[5]));
endmodule

module CPU_V2 (
);

  wire ALU_Calc, clock, DRW, JMP, reset;
  wire [2:0] ALU_co, DRID, flags, RS1ID;
  wire [3:0] ALU_OP;
  wire [22:0] bit_extender_1_out, PC_ip;
  wire [31:0] ALU_a_o, cpu_bus, SR1, SR2;

  Bit_Extender #(.in_width(32), .out_width(23), .\type ("zero")) bit_extender_1 (
    .in(cpu_bus), .out(bit_extender_1_out));
  ProgramCounter PC (.JmpAddr(bit_extender_1_out), .Reset(reset), .Jmp(JMP), .Clock(clock), .ip(PC_ip));
  assign cpu_bus = {{9{1'b0}}, PC_ip};  // Bit_Extender bit_extender_2
  ALU_V2 ALU (
    .C_or_B(1'b0), .Op(ALU_OP), .N1(SR1), .N2(SR1), .MC({32{1'b0}}), .CO(ALU_co[0]), .BO(ALU_co[1]),
    .A_O(ALU_a_o), .Comp(ALU_co[2]));  // open: MCO
  RegisterBank registerbank_1 (.RS1(RS1ID), .RS2(RS1ID), .DR(DRID), .W(DRW), .DRD(cpu_bus), .S1(SR1), .S2(SR2));
  Multiplexer #(.width(32)) multiplexer_1 (.in1(ALU_a_o), .out(cpu_bus), .sel(ALU_Calc));  // open: in0
  Register #(.width(3)) register_1 (.D(ALU_co), .en(ALU_Calc), .Q(flags));  // open: clk, clr
endmodule

module ALU_V2 (
  input  C_or_B,
  input  [3:0] Op,
  input  [31:0] N1,
  input  [31:0] N2,
  input  [31:0] MC,
  output CO,
  output BO,
  output [31:0] MCO,
  output [31:0] A_O,
  output Comp
);

  wire comparator_1_eq, comparator_1_gt, comparator_1_lt;
  wire [4:0] bit_extender_1_out, bit_extender_2_out, bit_extender_3_out, bit_extender_4_out,
       bit_extender_5_out;
  wire [31:0] adder_1_out, and_1_out, multiplier_1_out, negator_1_out, or_1_out, shifter_1_out,
       shifter_2_out, shifter_3_out, shifter_4_out, shifter_5_out, subtractor_1_out;

  Bit_Extender #(.in_width(32), .out_width(5), .\type ("zero")) bit_extender_1 (.in(N2), .out(bit_extender_1_out));
  Bit_Extender #(.in_width(32), .out_width(5), .\type ("zero")) bit_extender_2 (.in(N2), .out(bit_extender_2_out));
  Bit_Extender #(.in_width(32), .out_width(5), .\type ("zero")) bit_extender_3 (.in(N2), .out(bit_extender_3_out));
  Bit_Extender #(.in_width(32), .out_width(5), .\type ("zero")) bit_extender_4 (.in(N2), .out(bit_extender_4_out));
  Bit_Extender #(.in_width(32), .out_width(5), .\type ("zero")) bit_extender_5 (.in(N2), .out(bit_extender_5_out));
  Adder #(.width(32)) adder_1 (.a(N1), .b(N2), .out(adder_1_out), .cin(C_or_B), .cout(CO));
  Subtractor #(.width(32)) subtractor_1 (.a(N1), .b(N2), .out(subtractor_1_out), .bin(C_or_B), .bout(BO));
  Multiplier #(.width(32)) multiplier_1 (.a(N1), .b(N2), .out(multiplier_1_out), .cin(MC), .cout(MCO));
  Negator #(.width(32)) negator_1 (.in(N1), .out(negator_1_out));
  assign and_1_out = N1 & N2;  // AND_Gate and_1, 32 bits wide
  assign or_1_out = N1 | N2;  // OR_Gate or_1, 32 bits wide
  Shifter #(.width(32)) shifter_1 (.in(N1), .\dist (bit_extender_1_out), .out(shifter_1_out));
  Shifter #(.shift("lr"), .width(32)) shifter_2 (.in(N1), .\dist (bit_extender_2_out), .out(shifter_2_out));
  Shifter #(.shift("ar"), .width(32)) shifter_3 (.in(N1), .\dist (bit_extender_3_out), .out(shifter_3_out));
  Shifter #(.shift("rl"), .width(32)) shifter_4 (.in(N1), .\dist (bit_extender_4_out), .out(shifter_4_out));
  Shifter #(.shift("rr"), .width(32)) shifter_5 (.in(N1), .\dist (bit_extender_5_out), .out(shifter_5_out));
  Comparator #(.mode("unsigned"), .width(32)) comparator_1 (
    .a(N1), .b(N2), .gt(comparator_1_gt), .eq(comparator_1_eq), .lt(comparator_1_lt));
  Multiplexer #(.select(4), .width(32)) multiplexer_1 (
    .in0(adder_1_out), .in1(subtractor_1_out), .in2(multiplier_1_out), .in3(negator_1_out), .in4(and_1_out),
    .in5(or_1_out), .in6(shifter_1_out), .in7(shifter_2_out), .in8(shifter_3_out), .in9(shifter_4_out),
    .in10(shifter_5_out), .out(A_O), .sel(Op));  // open: in11, in12, in13, in14, in15
  Multiplexer #(.select(4)) multiplexer_2 (
    .in0(comparator_1_gt), .in1(comparator_1_eq), .in2(comparator_1_lt), .out(Comp), .sel(Op));  // open: in3, in4, in5, in6, in7, in8, in9, in10, in11, in12, in13, in14, in15
endmodule

module RegisterBank (
  input  [2:0] RS1,
  input  [2:0] RS2,
  input  [2:0] DR,
  input  W,
  input  [31:0] DRD,
  output [31:0] S1,
  output [31:0] S2
);

  wire and_1_out, decoder_1_out0, decoder_1_out1, decoder_1_out2, decoder_1_out3, decoder_1_out4,
       decoder_1_out5, decoder_1_out6, decoder_1_out7;
  wire [31:0] R0_q, R1_q, R2_q, R3_q, R4_q, R5_q, R6_q, R7_q;

  Decoder #(.select(3)) decoder_1 (
    .out0(decoder_1_out0), .out1(decoder_1_out1), .out2(decoder_1_out2), .out3(decoder_1_out3),
    .out4(decoder_1_out4), .out5(decoder_1_out5), .out6(decoder_1_out6), .out7(decoder_1_out7), .sel(DR),
    .en(1'b1));
  and and_1 (and_1_out, W, decoder_1_out0);
  Register #(.width(32)) R0 (.D(DRD), .en(and_1_out), .Q(R0_q));  // open: clk, clr
  Register #(.width(32)) R1 (.D(DRD), .en(decoder_1_out1), .Q(R1_q));  // open: clk, clr
  Register #(.width(32)) R2 (.D(DRD), .en(decoder_1_out2), .Q(R2_q));  // open: clk, clr
  Register #(.width(32)) R3 (.D(DRD), .en(decoder_1_out3), .Q(R3_q));  // open: clk, clr
  Register #(.width(32)) R4 (.D(DRD), .en(decoder_1_out4), .Q(R4_q));  // open: clk, clr
  Register #(.width(32)) R5 (.D(DRD), .en(decoder_1_out5), .Q(R5_q));  // open: clk, clr
  Register #(.width(32)) R6 (.D(DRD), .en(decoder_1_out6), .Q(R6_q));  // open: clk, clr
  Register #(.width(32)) R7 (.D(DRD), .en(decoder_1_out7), .Q(R7_q));  // open: clk, clr
  Multiplexer #(.select(3), .width(32)) multiplexer_1 (
    .in0(R0_q), .in1(R1_q), .in2(R2_q), .in3(R3_q), .in4(R4_q), .in5(R5_q), .in6(R6_q), .in7(R7_q), .out(S1),
    .sel(RS1));
  Multiplexer #(.select(3), .width(32)) multiplexer_2 (
    .in0(R0_q), .in1(R1_q), .in2(R2_q), .in3(R3_q), .in4(R4_q), .in5(R5_q), .in6(R6_q), .in7(R7_q), .out(S2),
    .sel(RS2));
endmodule

module InstrDecoderV2 (
  input  [31:0] in_1,
  output [3:0] ALUOPCode,
  output [2:0] R3,
  output [2:0] R2,
  output [2:0] R1,
  output NOP,
  output ALUCalc,
  output ALUCOMP,
  output JMP,
  output [1:0] JifFrm,
  output ST,
  output LD,
  output LDI,
  output MOV,
  output IOC,
  output Error,
  output [23:0] IRV
);

  wire and_1_out, decoder_1_out9, decoder_1_out10, decoder_1_out11, decoder_1_out12, decoder_1_out13,
       decoder_1_out14, decoder_1_out15, decoder_1_out16, decoder_1_out17, decoder_1_out18, decoder_1_out19,
       decoder_1_out20, decoder_1_out21, decoder_1_out22, decoder_1_out23, decoder_1_out24, decoder_1_out25,
       decoder_1_out26, decoder_1_out27, decoder_1_out28, decoder_1_out29, decoder_1_out30, decoder_1_out31,
       or_2_out;
  wire [2:0] multiplexer_2_out;

  Decoder #(.enable("false"), .select(5)) decoder_1 (
    .out0(NOP), .out1(ALUCalc), .out2(ALUCOMP), .out3(JMP), .out4(ST), .out5(LD), .out6(LDI), .out7(MOV),
    .out8(IOC), .out9(decoder_1_out9), .out10(decoder_1_out10), .out11(decoder_1_out11),
    .out12(decoder_1_out12), .out13(decoder_1_out13), .out14(decoder_1_out14), .out15(decoder_1_out15),
    .out16(decoder_1_out16), .out17(decoder_1_out17), .out18(decoder_1_out18), .out19(decoder_1_out19),
    .out20(decoder_1_out20), .out21(decoder_1_out21), .out22(decoder_1_out22), .out23(decoder_1_out23),
    .out24(decoder_1_out24), .out25(decoder_1_out25), .out26(decoder_1_out26), .out27(decoder_1_out27),
    .out28(decoder_1_out28), .out29(decoder_1_out29), .out30(decoder_1_out30), .out31(decoder_1_out31),
    .sel(in_1[4:0]));
  or or_1 (Error, decoder_1_out9, decoder_1_out10, decoder_1_out11, decoder_1_out12, decoder_1_out13, decoder_1_out14, decoder_1_out15, decoder_1_out16, decoder_1_out17, decoder_1_out18, decoder_1_out19, decoder_1_out20, decoder_1_out21, decoder_1_out22, decoder_1_out23, decoder_1_out24, decoder_1_out25, decoder_1_out26, decoder_1_out27, decoder_1_out28, decoder_1_out29, decoder_1_out30, decoder_1_out31);
  Multiplexer #(.width(4)) multiplexer_1 (.in0(in_1[17:14]), .in1(in_1[8:5]), .out(ALUOPCode), .sel(ALUCOMP));
  Multiplexer #(.width(3)) multiplexer_2 (.in0(in_1[7:5]), .in1(in_1[10:8]), .out(multiplexer_2_out), .sel(and_1_out));
  and and_1 (and_1_out, in_1[5], JMP);
  or or_2 (or_2_out, LDI, LD);
  Multiplexer #(.width(3)) multiplexer_3 (.in0(multiplexer_2_out), .in1(in_1[13:11]), .out(R1), .sel(or_2_out));

  assign IRV = in_1[31:8];
  assign JifFrm = in_1[7:6];
  assign R2 = in_1[10:8];
  assign R3 = in_1[13:11];
endmodule
